# Fritzing sketch pacman (saved by Fritzing 0.9.1b)
breadboards: 1

parts:
  Part1 = Arduino Leonardo (Rev3b)
  R3 = Resistor [tolerance=±5% resistance=220 package=THT]
  R1 = Resistor [tolerance=±5% resistance=220 package=THT]
  R2 = Resistor [tolerance=±5% resistance=220 package=THT]
  R4 = Resistor [tolerance=±5% resistance=220 package=THT]

nets:
  N1: Part1.GND, R3.Pin_1, R2.Pin_1, R4.Pin_1
  N2: Part1.A1, R2.Pin_0
  N3: Part1.A2, R1.Pin_0
  N4: Part1.A3, R3.Pin_0
  N5: Part1.A4, R4.Pin_0

notes:
  connect me
